# Fritzing sketch z80 (saved by Fritzing 0.9.3b)
circuit board: 12.3581cm x 6.30581cm
breadboards: 1

parts:
  Part1 = Arduino Uno (Rev3)
  IC1 = Z80 A [package="DIP (Dual Inline) [THT]"]

nets:
  N1: Part1.D8, IC1.D6
  N2: Part1.D9_PWM, IC1.D7
  N3: Part1.D11_PWM/MOSI, IC1.CLK
  N4: Part1.D2, IC1.D0
  N5: Part1.D3_PWM, IC1.D1
  N6: Part1.D4, IC1.D2
  N7: Part1.D5_PWM, IC1.D3
  N8: Part1.D6_PWM, IC1.D4
  N9: Part1.D7, IC1.D5
  N10: Part1.RESET, IC1.!_RESET
  5V: Part1.5V, IC1.+5V
  GND: Part1.GND, IC1.A11, IC1.A12, IC1.A13, IC1.A14, IC1.A15, IC1.GND, IC1.A0, IC1.A1, IC1.A2, IC1.A3, IC1.A4, IC1.A5, IC1.A6, IC1.A7, IC1.A8, IC1.A9, IC1.A10

custom parts:
  Z80 A: Zilog Z80 A CPU
